# Fritzing sketch Examp1 (saved by Fritzing 0.9.9b)
circuit board: 8.46667cm x 5.64444cm
breadboards: 1

parts:
  Компонент1 = Arduino Uno (Rev3)
  LED1 = LED - 5mm [color="Yellow (595nm)" current=30mA package="5 mm [THT]"]
  R1 = Resistor [tolerance=±5% power=0.25 resistance=240 package=THT]

nets:
  N1: Компонент1.D9_PWM, R1.Pin_1
  N2: Компонент1.GND, LED1.cathode
  N3: LED1.anode, R1.Pin_0

// code stored in the sketch: Examp1.fzz.ino
/*
Exploring Arduino - Code Listing 2-2: LED with Changing Blink Rate
http://www.exploringarduino.com/content/ch2

Copyright 2013 Jeremy Blum ( http://www.jeremyblum.com )
This program is free software: you can redistribute it and/or modify
it under the terms of the GNU General Public License v3 as published by
the Free Software Foundation.
*/

const int LED=9;         //define LED for Pin 9
void setup()
{
  pinMode (LED, OUTPUT); //Set the LED pin as an output
}

void loop()
{
  for (int i=100; i<=1000; i=i+100)
  {
    digitalWrite(LED, HIGH);
    delay(i);
    digitalWrite(LED, LOW);
    delay(i);
  }
}
