# Fritzing sketch 02-StjagRes (saved by Fritzing 0.9.9b)
circuit board: 10.4425cm x 6.92774cm
breadboards: 1

parts:
  Компонент1 = Arduino Uno (Rev3)
  LED1 = LED - 5mm [color="Red (633nm)" current=0.030 package="5 mm [THT]"]
  R1 = Resistor [tolerance=±5% power=0.25 resistance=220 package=THT]
  R2 = Resistor [tolerance=±5% power=0.25 resistance=10k package=THT]
  S1 = Pushbutton [package="[THT]"]

nets:
  N1: Компонент1.D9_PWM, R1.Pin_0
  N2: Компонент1.D2, R2.Pin_0, S1.Pin_1, S1.Pin_2
  N3: Компонент1.5V, S1.Pin_3, S1.Pin_4
  N4: Компонент1.GND, LED1.cathode, R2.Pin_1
  N5: LED1.anode, R1.Pin_1
