# Fritzing sketch 03-poti (saved by Fritzing 0.9.9b)
circuit board: 8.62697cm x 7.21919cm
breadboards: 1

parts:
  Компонент1 = Arduino Uno (Rev3)
  R2 = Rotary Potentiometer (Small) [maximum_resistance=10kΩ package=THT]

nets:
  N1: Компонент1.A0, R2.wiper
  N2: Компонент1.5V, R2.leg2
  N3: Компонент1.GND, R2.leg1

// code stored in the sketch: 03-pot.ino
/*
Exploring Arduino - Code Listing 3-1: Potentiometer Reading Sketch
http://www.exploringarduino.com/content/ch3
стр.63-70
Copyright 2013 Jeremy Blum ( http://www.jeremyblum.com )
This program is free software: you can redistribute it and/or modify
it under the terms of the GNU General Public License v3 as published by
the Free Software Foundation.
*/

//Potentiometer Reading Program

const int POT=0;  //Pot on Analog Pin 0
int val = 0;      //variable to hold the analog reading from the POT

void setup()
{
  Serial.begin(9600);
}

void loop()
{
  val = analogRead(POT);
  Serial.println(val);
  delay(500);
}
