# Fritzing sketch 04-CameraTrap (saved by Fritzing 0.9.9b)
breadboards: 1

parts:
  Mod1 = ESP32 - CAM
  Компонент1 = Arduino Pro Mini v13  # not connected
  VCC1 = Battery
  Компонент2 = USB converter CP2102

nets:
  5V: Mod1.5V, VCC1.+, Компонент2.+5V
  GND: Mod1.GND, Mod1.IO0, VCC1.-, Компонент2.GND

custom parts:
  ESP32 - CAM: The ESP32-CAM has a very competitive small-size camera module that can operate independently as a minimum system with a footprint of only 27*40.5*4.5mm and a deep sleep current of up to 6mA.
