# Fritzing sketch ESP32-SDcard (saved by Fritzing 1.0.2b)
breadboards: 1

parts:
  U1 = ESP32-38PinWide [part_number=ESP32-38PinWide]
  MH-SD_Card_Module1 = MH-SD_Card_Module [part_number=002]

nets:
  N1: U1.GPIO11, MH-SD_Card_Module1.connector7
  N2: U1.VIN, MH-SD_Card_Module1.connector5
  N3: U1.GPIO5, MH-SD_Card_Module1.connector4
  N4: U1.GPIO18, MH-SD_Card_Module1.connector2
  N5: U1.GPIO19, MH-SD_Card_Module1.connector1
  N6: U1.GPIO23, MH-SD_Card_Module1.connector3

custom parts:
  ESP32-38PinWide: Generic 38-Pin ESP32 with wide format (only access to one side of pins on a breadboard) based on Stephen Lilley's HiLetgo ESP-WROOM-32 ESP32 ESP-32S Development Board.
