# Fritzing sketch HC-SR501-proba (saved by Fritzing 1.0.2b)
breadboards: 1

parts:
  Компонент1 = HC-SR501 Body Sensor Module
  Компонент2 = Arduino Uno (Rev3)
  LED1 = LED - 5mm [color="Red (633nm)" current=0.030A package="5 mm [THT]"]
  LED2 = LED - 5mm [color="Yellow (592nm)" current=0.030A package="5 mm [THT]"]
  LED3 = LED - 5mm [color="Green (570nm)" current=0.030A package="5 mm [THT]"]
  R1 = Resistor [tolerance=±5% power=0.25W resistance=330 package=THT]
  R2 = Resistor [tolerance=±5% power=0.25W resistance=330 package=THT]
  R3 = Resistor [tolerance=±5% power=0.25W resistance=330 package=THT]

nets:
  VCC: Компонент1.VCC, Компонент2.5V
  N1: Компонент1.OUT, Компонент2.D7
  GND: Компонент1.GND, Компонент2.GND, LED1.cathode, LED2.cathode, LED3.cathode
  N2: Компонент2.D11_PWM/MOSI, R1.Pin_1
  N3: Компонент2.D12/MISO, R2.Pin_1
  N4: Компонент2.D13/SCK, R3.Pin_1
  N5: LED1.anode, R1.Pin_0
  N6: LED2.anode, R2.Pin_0
  N7: LED3.anode, R3.Pin_0

custom parts:
  HC-SR501 Body Sensor Module: Pyroelectric Infrared PIR Motion Sensor Detector Module
